# Fritzing sketch Fritzing (saved by Fritzing 0.9.3b)
breadboards: 1

parts:
  HC-SR04_Sensor_1 = HC-SR04 Ultrasonic Distance Sensor
  S1 = H-Bridge with L298N
  Espessif_Serial_Wifi_Modul_1 = ESP8266 ESP01 [part_number=ESP8266 package=THT]
  M1 = DC Motor
  부품1 = Soil Moisture Sensor
  R1 = PHOTOCELL [package=photocell]
  부품2 = Arduino Uno (Rev3)
  DHT2 = DHT11 Humitidy and Temperature Sensor (3 pins)
  o1 = Module display OLED I2C 128x64 SSD1306 [package=THT]
  R2 = Resistor [tolerance=±5% resistance=220 package=THT]
  M2 = DC Motor

nets:
  VCC: HC-SR04_Sensor_1.VCC, 부품1.VCC, R1.P$2, 부품2.5V, DHT2.VDD, o1.VCC
  N1: HC-SR04_Sensor_1.TRIG, 부품2.D11_PWM/MOSI
  N2: HC-SR04_Sensor_1.ECHO, 부품2.D12/MISO
  GND: HC-SR04_Sensor_1.GND, S1.GND, Espessif_Serial_Wifi_Modul_1.GND, 부품1.GND, 부품2.GND, DHT2.GND, o1.GND, R2.Pin_0
  N3: S1.ENA, 부품2.D8
  N4: S1.IN1, 부품2.D7
  N5: S1.IN2, 부품2.D6_PWM
  N6: S1.IN3, 부품2.D5_PWM
  N7: S1.IN4, 부품2.D4
  N8: S1.ENB, 부품2.D3_PWM
  N9: S1.M1-01, M1.pin_2
  N10: S1.M1-02, M1.pin_1
  N11: S1.M2-01, M2.pin_2
  N12: S1.M2-02, M2.pin_1
  N13: Espessif_Serial_Wifi_Modul_1.RXD, 부품2.D1/TX
  N14: Espessif_Serial_Wifi_Modul_1.TXD, 부품2.D0/RX
  VCC_2: Espessif_Serial_Wifi_Modul_1.VCC, Espessif_Serial_Wifi_Modul_1.CH_PD, 부품2.3V3
  N15: 부품1.SIG, 부품2.D10_PWM/SS
  N16: R1.P$1, 부품2.A0, R2.Pin_1
  N17: 부품2.A4/SDA, o1.SDA
  N18: 부품2.A5/SCL, o1.SCL
  N19: 부품2.D2, DHT2.DATA

custom parts:
  H-Bridge with L298N: h-bridge
  ESP8266 ESP01: Generic WiFi Module based on the ESP8266 with onboard PCB antenna and UART communications
  DHT11 Humitidy and Temperature Sensor (3 pins): DHT11 Humidity and Temperature Sensor (3 pins) from the design created by John De Cristofaro for Adafruit Industries.
  Module display OLED I2C 128x64 SSD1306: Ecran OLED I2C SSD163 de 128x64 avec connexion I2C
