# Fritzing sketch Fritzing1 (saved by Fritzing 0.9.3b)
breadboards: 1

parts:
  U1 = NodeMCU V1.0
  S1 = H-Bridge with L298N
  M1 = DC Motor
  M2 = DC Motor
  부품1 = Soil Moisture Sensor
  hc-sr1 = hc-sr04
  DHT1 = DHT11 Humitidy and Temperature Sensor (3 pins)
  부품2 = Arduino Uno (Rev3)
  Espessif_Serial_Wifi_Modul_1 = ESP8266 ESP01 [part_number=ESP8266 package=THT]
  부품3 = Soil Moisture Sensor
  o1 = Module display OLED I2C 128x64 SSD1306 [package=THT]
  U2 = 74HC595 [package="DIP16 [THT]"]  # not connected

nets:
  N1: U1.D1, o1.SCL
  N2: U1.D2, o1.SDA
  N3: U1.D4, DHT1.DATA
  3V3: U1.3V3, DHT1.VDD
  GND: U1.GND, DHT1.GND
  N4: S1.ENA, 부품2.D5_PWM
  N5: S1.ENB, 부품2.D3_PWM
  N6: S1.M1-01, M2.pin_1
  N7: S1.M1-02, M2.pin_2
  N8: S1.M2-01, M1.pin_2
  N9: S1.M2-02, M1.pin_1
  VCC: 부품1.VCC, hc-sr1.VCC, 부품2.5V, 부품3.VCC, o1.VCC
  N10: 부품1.SIG, 부품2.A1
  GND_2: 부품1.GND, hc-sr1.GND, 부품2.GND, Espessif_Serial_Wifi_Modul_1.GND, 부품3.GND, o1.GND
  N11: hc-sr1.Trig, 부품2.D8
  N12: hc-sr1.Echo, 부품2.D7
  N13: 부품2.A0, 부품3.SIG
  N14: 부품2.D0/RX, Espessif_Serial_Wifi_Modul_1.TXD
  N15: 부품2.D1/TX, Espessif_Serial_Wifi_Modul_1.RXD
  3V3_2: 부품2.3V3, Espessif_Serial_Wifi_Modul_1.VCC

custom parts:
  NodeMCU V1.0: ESP8266 based NodeMCU
  H-Bridge with L298N: h-bridge
  DHT11 Humitidy and Temperature Sensor (3 pins): DHT11 Humidity and Temperature Sensor (3 pins) from the design created by John De Cristofaro for Adafruit Industries.
  ESP8266 ESP01: Generic WiFi Module based on the ESP8266 with onboard PCB antenna and UART communications
  Module display OLED I2C 128x64 SSD1306: Ecran OLED I2C SSD163 de 128x64 avec connexion I2C
